# Fritzing sketch Fritz_Alarm_Buzzer (saved by Fritzing 0.9.10b)
breadboards: 1

parts:
  LED1 = smd LED [color="Red (633nm)" package="1206 [SMD]"]
  LED2 = smd LED [color="Blue (470nm)" package="1206 [SMD]"]
  R1 = Resistor [tolerance=±5% power=0.25 resistance=220 package=THT]
  R2 = Resistor [tolerance=±5% power=0.25 resistance=220 package=THT]
  Part1 = Arduino Uno (Rev3)
  J1 = Piezo Speaker

nets:
  N1: LED1.cathode, R1.Pin_0
  N2: LED1.anode, Part1.D4
  N3: LED2.cathode, R2.Pin_0
  N4: LED2.anode, Part1.D2
  N5: R1.Pin_1, R2.Pin_1, Part1.GND, J1.pin1
  N6: Part1.D9_PWM, J1.pin2
