# Fritzing sketch FRITZ_COMPLETE (saved by Fritzing 0.9.10b)
breadboards: 2

parts:
  Part1 = Arduino Uno (Rev3)
  Mod1 = Amica NodeMCU DEVKIT 1.0
  LCD1 = LCD screen
  LCM1602_IIC1 = LCM1602 IIC [part_number="LCM1602 IIC" chip_label="LCM1602 IIC" package="DIP (Dual Inline) [THT]"]
  Keypad4x1 = Keypad Membran 4x4
  Part2 = RFID-RC522-v2
  Part3 = HC-SR501 Body Sensor Module
  Part4 = HC-SR501 Body Sensor Module
  LED1 = smd LED [color="White (4500K)" package="1206 [SMD]"]
  R1 = PHOTOCELL [package=photocell]
  R2 = Resistor [tolerance=±5% resistance=220 package="2010 [SMD]"]
  R3 = Resistor [tolerance=±5% resistance=220 package="2010 [SMD]"]
  LED2 = smd LED [color="Green (555nm)" package="1206 [SMD]"]
  R4 = Resistor [tolerance=±5% resistance=220 package="2010 [SMD]"]
  D1 = Zener Diode [part_number=1N4732A breakdown_voltage=3.6V package="300 mil [THT]"]
  J1 = Basic Servo
  VCC1 = Battery block 9V
  buz1 = Piezo Buzzer
  LED3 = smd LED [color="Red (633nm)" package="1206 [SMD]"]
  R5 = Resistor [tolerance=±5% resistance=220 package="2010 [SMD]"]

nets:
  N1: Part1.A4/SDA, Mod1.pin_13, LCM1602_IIC1.SDA
  N2: Part1.A5/SCL, Mod1.pin_14, LCM1602_IIC1.SCL
  N3: Part1.D8, Keypad4x1.Pin5
  N4: Part1.D9_PWM, Keypad4x1.Pin4
  N5: Part1.D10_PWM/SS, Keypad4x1.Pin3
  N6: Part1.D11_PWM/MOSI, Keypad4x1.Pin2
  N7: Part1.D12/MISO, Keypad4x1.Pin1
  N8: Part1.D13/SCK, LED3.anode
  N9: Part1.D2, buz1.pin_1
  N10: Part1.D3_PWM, J1.pulse
  N11: Part1.D4, LED1.anode
  N12: Part1.D5_PWM, LED2.anode
  N13: Part1.D6_PWM, Keypad4x1.Pin7
  N14: Part1.D7, Keypad4x1.Pin6
  N15: Mod1.pin1, Mod1.pin_10, Mod1.pin_26
  GND: Mod1.pin2, Mod1.pin_9, Mod1.pin_25, Mod1.pin_29, LCM1602_IIC1.GND, Part2.GND, Part3.GND, Part4.GND, R2.Pin_1, R3.Pin_1, R4.Pin_1, buz1.pin_2, R5.Pin_0
  N16: Mod1.pin5, Part2.RST
  N17: Mod1.pin6, Part2.MOSI
  N18: Mod1.pin7, Part2.MISO
  N19: Mod1.pin8, Part2.SCK
  N20: Mod1.pin_11, Part2.SDA
  N21: Mod1.pin_12, Part3.OUT
  N22: Mod1.pin_15, Part4.OUT
  N23: Mod1.pin_16, R1.P$2, R4.Pin_0
  VSS: LCD1.VSS, LCM1602_IIC1.VSS
  VDD: LCD1.VDD, LCM1602_IIC1.VDD
  N24: LCD1.V0, LCM1602_IIC1.V0
  N25: LCD1.RS, LCM1602_IIC1.RS
  N26: LCD1.R/W, LCM1602_IIC1.RW
  N27: LCD1.E, LCM1602_IIC1.E
  N28: LCD1.DB0, LCM1602_IIC1.D0
  N29: LCD1.DB1, LCM1602_IIC1.D1
  N30: LCD1.DB2, LCM1602_IIC1.D2
  N31: LCD1.DB3, LCM1602_IIC1.D3
  N32: LCD1.DB4, LCM1602_IIC1.D4
  N33: LCD1.DB5, LCM1602_IIC1.D5
  N34: LCD1.DB6, LCM1602_IIC1.D6
  N35: LCD1.DB7, LCM1602_IIC1.D7
  N36: LCD1.LED+, LCM1602_IIC1.A
  N37: LCD1.LED-, LCM1602_IIC1.K
  VCC: LCM1602_IIC1.VCC, Part2.3.3V
  N38: LCM1602_IIC1.LED_A, LCM1602_IIC1.LED_B
  VCC_2: Part3.VCC, Part4.VCC, R1.P$1
  N39: LED1.cathode, R2.Pin_0
  N40: R3.Pin_0, LED2.cathode
  N41: D1.cathode, VCC1.+
  N42: D1.anode, VCC1.-
  N43: LED3.cathode, R5.Pin_1

custom parts:
  LCM1602 IIC: I2C-Module to use a 1602 or 2004 LCD on with the wire.h libory Serial LCD Modul
  Keypad Membran 4x4: Membrane Keypad 4x4 Matrix
  RFID-RC522-v2: A simple China made RFID-RC522 Reader; do check the pin labels, as this is a MFRC522 based clone.
  HC-SR501 Body Sensor Module: Pyroelectric Infrared PIR Motion Sensor Detector Module
  Piezo Buzzer: Part from https://www.nutsvolts.com/magazine/article/november2012_SmileysWorkshop. Breadboard and icon images modified to be 0.3" in spacing and be more similar to the actual physical part.
