# Fritzing sketch Fritz_lysresistor (saved by Fritzing 0.9.10b)
breadboards: 1

parts:
  LED1 = smd LED [color="Blue (470nm)" package="1206 [SMD]"]
  LED2 = smd LED [color="White (4500K)" package="1206 [SMD]"]
  Part1 = Arduino Uno (Rev3)
  Mod1 = Amica NodeMCU DEVKIT 1.0
  R1 = PHOTOCELL [package=photocell]
  R2 = Resistor [tolerance=±5% power=0.25 resistance=220 package=THT]
  R3 = Resistor [tolerance=±5% power=0.25 resistance=220 package=THT]
  R4 = Resistor [tolerance=±5% power=0.25 resistance=220 package=THT]

nets:
  N1: LED1.cathode, R4.Pin_0
  N2: LED1.anode, Part1.D12/MISO
  N3: LED2.cathode, R3.Pin_0
  N4: LED2.anode, Part1.D11_PWM/MOSI
  N5: Part1.A4/SDA, Mod1.pin_13
  N6: Part1.A5/SCL, Mod1.pin_14
  N7: Part1.GND, Mod1.pin2, R2.Pin_1, R3.Pin_1, R4.Pin_1
  N8: Mod1.pin_16, R1.P$1, R2.Pin_0
