# Fritzing sketch LightSensor_with_LED_Fritzing (saved by Fritzing 0.9.10b)
breadboards: 1

parts:
  R1 = Photocell (LDR) [package=THT]
  R2 = Resistor [tolerance=±5% power=0.25 resistance=220 package=THT]
  R3 = Resistor [tolerance=±5% power=0.25 resistance=220 package=THT]
  Part1 = Arduino Uno (Rev3) - ICSP
  LED1 = LED - 5mm [color="Red (633nm)" current=0.030 package="5 mm [THT]"]

nets:
  N1: R1.pin_1, R3.Pin_1, Part1.A0
  N2: R2.Pin_0, R3.Pin_0
  N3: R2.Pin_1, LED1.cathode
  N4: Part1.D9_PWM, LED1.anode
