# Fritzing sketch ServoMotor_Fritzing (saved by Fritzing 0.9.10b)
breadboards: 1

parts:
  D1 = Rectifier Diode [part_number=1N4001 package="300 mil [THT]"]
  Mod1 = Amica NodeMCU DEVKIT 1.0
  J1 = Basic Servo

nets:
  N1: D1.cathode, Mod1.pin_30, J1.vcc
  N2: D1.anode, Mod1.pin_9, Mod1.pin_25, Mod1.pin_29, J1.gnd
  N3: Mod1.pin_12, J1.pulse
