# Fritzing sketch MotionSensorFritzing (saved by Fritzing 0.9.10b)
breadboards: 1

parts:
  Motion_Sensor_HC-SR501 = HC-SR501 Body Sensor Module
  Mod1 = Amica NodeMCU DEVKIT 1.0
  Motion_Sensor_HC-SR501_2 = HC-SR501 Body Sensor Module
  5V_-_12V = BC9VPC [package=bc9vpc]

nets:
  VCC: Motion_Sensor_HC-SR501.VCC, Motion_Sensor_HC-SR501_2.VCC, 5V_-_12V.V+
  N1: Motion_Sensor_HC-SR501.OUT, Mod1.pin_12
  GND: Motion_Sensor_HC-SR501.GND, Mod1.pin_9, Mod1.pin_25, Mod1.pin_29, Motion_Sensor_HC-SR501_2.GND
  N2: Mod1.pin_15, Motion_Sensor_HC-SR501_2.OUT

custom parts:
  HC-SR501 Body Sensor Module: Pyroelectric Infrared PIR Motion Sensor Detector Module
