# Fritzing sketch LightSensor_with_LED_Fritzing (saved by Fritzing 0.9.10b)
breadboards: 1

parts:
  R1 = Photocell (LDR) [package=THT]
  R2 = Resistor [tolerance=±5% power=0.25 resistance=220 package=THT]
  R3 = Resistor [tolerance=±5% power=0.25 resistance=220 package=THT]
  Part1 = Arduino Uno (Rev3) - ICSP
  LED2 = LED - 5mm [color="Blue (430nm)" current=0.030 package="5 mm [THT]"]
  R4 = Resistor [tolerance=±5% power=0.25 resistance=220 package=THT]
  LED3 = LED - 5mm [color="Red (633nm)" current=0.030 package="5 mm [THT]"]

nets:
  N1: R1.pin_0, Part1.5V
  N2: R1.pin_1, R3.Pin_1, Part1.A0
  N3: R2.Pin_0, R3.Pin_0, Part1.GND, R4.Pin_0
  N4: R2.Pin_1, LED3.cathode
  N5: Part1.D8, LED2.anode
  N6: Part1.D9_PWM, LED3.anode
  N7: LED2.cathode, R4.Pin_1
