# Fritzing sketch Master_Slave_Example_Fritzing (saved by Fritzing 0.9.10b)
breadboards: 1

parts:
  MASTER_ESP8266 = Amica NodeMCU DEVKIT 1.0
  SLAVE_Arduino_UNO = Arduino Uno (Rev3)
  R1 = Resistor [tolerance=±5% power=0.25 resistance=330 package=THT]
  LED1 = LED - 5mm [color="Red (633nm)" current=0.030 package="5 mm [THT]"]
  R2 = Resistor [tolerance=±5% power=0.25 resistance=330 package=THT]
  LED2 = LED - 5mm [color="Green (555nm)" current=0.030 package="5 mm [THT]"]

nets:
  N1: MASTER_ESP8266.pin1, MASTER_ESP8266.pin_10, MASTER_ESP8266.pin_26
  N2: MASTER_ESP8266.pin2, MASTER_ESP8266.pin_9, MASTER_ESP8266.pin_25, MASTER_ESP8266.pin_29, SLAVE_Arduino_UNO.GND, R1.Pin_0, R2.Pin_0
  N3: MASTER_ESP8266.pin_13, SLAVE_Arduino_UNO.A4/SDA
  N4: MASTER_ESP8266.pin_14, SLAVE_Arduino_UNO.A5/SCL
  N5: SLAVE_Arduino_UNO.D8, LED2.anode
  N6: SLAVE_Arduino_UNO.D9_PWM, LED1.anode
  N7: R1.Pin_1, LED1.cathode
  N8: R2.Pin_1, LED2.cathode
